// Logisim project EX1.circ as structural Verilog
module somador (
  input  A0,
  input  B0,
  output soma,
  output carry_out
);

  xor xor_1 (soma, A0, B0);
  and and_1 (carry_out, A0, B0);
endmodule

// decodf
module decodificador (
  input  h,
  input  x2,
  input  x3,
  input  x4,
  output a,
  output b,
  output c,
  output d,
  output e,
  output f,
  output g
);

  wire and_1_out, and_2_out, and_3_out, and_4_out, and_5_out, and_6_out, and_7_out, and_8_out, and_9_out,
       and_10_out, and_11_out, and_12_out, and_13_out, and_14_out, and_15_out, and_16_out, and_17_out,
       and_18_out, and_19_out, and_20_out, and_21_out, and_22_out, and_23_out, and_24_out, and_25_out,
       and_26_out, and_27_out, and_28_out, and_29_out, and_30_out, and_31_out, and_32_out, and_33_out,
       and_34_out, and_35_out, and_36_out, and_37_out, and_38_out, and_39_out, and_40_out, and_41_out,
       and_42_out, and_43_out, and_44_out, and_45_out, and_46_out, and_47_out, and_48_out, and_49_out,
       not_1_out, not_2_out, not_3_out, not_4_out, not_5_out, not_6_out, not_7_out, not_8_out, not_9_out,
       not_10_out, not_11_out, not_12_out, not_13_out, not_14_out, not_15_out, not_16_out, not_17_out,
       not_18_out, not_19_out, not_20_out, not_21_out, not_22_out, not_23_out, not_24_out, not_25_out,
       not_26_out, not_27_out, not_28_out, not_29_out, not_30_out, not_31_out, not_32_out, not_33_out,
       not_34_out, not_35_out, not_36_out, not_37_out, not_38_out, not_39_out, not_40_out, not_41_out,
       not_42_out, not_43_out, not_44_out, not_45_out, or_1_out, or_2_out, or_3_out, or_4_out, or_5_out,
       or_6_out, or_7_out, or_8_out, or_9_out, or_10_out, or_12_out, or_13_out, or_14_out, or_15_out,
       or_16_out, or_17_out, or_18_out, or_20_out, or_21_out, or_22_out, or_23_out;

  not not_1 (not_1_out, x2);
  not not_2 (not_2_out, x4);
  not not_3 (not_3_out, h);
  and and_1 (and_1_out, not_3_out, not_4_out);
  not not_4 (not_4_out, x2);
  not not_5 (not_5_out, h);
  and and_2 (and_2_out, h, not_6_out);
  not not_6 (not_6_out, x2);
  not not_7 (not_7_out, x3);
  not not_8 (not_8_out, x4);
  not not_9 (not_9_out, h);
  not not_10 (not_10_out, x2);
  not not_11 (not_11_out, h);
  and and_3 (and_3_out, not_11_out, not_12_out);
  not not_12 (not_12_out, x3);
  not not_13 (not_13_out, x4);
  not not_14 (not_14_out, h);
  not not_15 (not_15_out, x3);
  not not_16 (not_16_out, h);
  and and_4 (and_4_out, not_16_out, not_17_out);
  not not_17 (not_17_out, x3);
  not not_18 (not_18_out, h);
  and and_5 (and_5_out, not_18_out, x4);
  not not_19 (not_19_out, x3);
  not not_20 (not_20_out, h);
  not not_21 (not_21_out, x2);
  not not_22 (not_22_out, h);
  and and_6 (and_6_out, not_22_out, not_23_out);
  not not_23 (not_23_out, x2);
  not not_24 (not_24_out, x4);
  not not_25 (not_25_out, x2);
  and and_7 (and_7_out, not_25_out, x3);
  not not_26 (not_26_out, x3);
  not not_27 (not_27_out, x3);
  not not_28 (not_28_out, x2);
  and and_8 (and_8_out, not_28_out, not_29_out);
  not not_29 (not_29_out, x4);
  and and_9 (and_9_out, x3, not_30_out);
  not not_30 (not_30_out, x4);
  and and_10 (and_10_out, h, x3);
  and and_11 (and_11_out, h, x2);
  not not_31 (not_31_out, x3);
  not not_32 (not_32_out, x4);
  not not_33 (not_33_out, h);
  and and_12 (and_12_out, not_33_out, x2);
  not not_34 (not_34_out, x3);
  not not_35 (not_35_out, x2);
  and and_13 (and_13_out, not_35_out, x3);
  and and_14 (and_14_out, x3, not_36_out);
  not not_36 (not_36_out, x4);
  not not_37 (not_37_out, h);
  and and_15 (and_15_out, not_37_out, x2);
  not not_38 (not_38_out, x3);
  not not_39 (not_39_out, x2);
  and and_16 (and_16_out, not_1_out, not_2_out);
  and and_17 (and_17_out, and_1_out, x3);
  and and_18 (and_18_out, not_5_out, x2);
  and and_19 (and_19_out, and_2_out, not_7_out);
  and and_20 (and_20_out, h, not_8_out);
  and and_21 (and_21_out, h, x2);
  and and_22 (and_22_out, not_9_out, not_10_out);
  and and_23 (and_23_out, and_3_out, not_13_out);
  not not_40 (not_40_out, x2);
  not not_41 (not_41_out, x4);
  and and_24 (and_24_out, not_14_out, x3);
  and and_25 (and_25_out, h, not_15_out);
  or or_1 (or_1_out, and_4_out, and_5_out);
  and and_26 (and_26_out, not_19_out, x4);
  and and_27 (and_27_out, not_20_out, x2);
  and and_28 (and_28_out, h, not_21_out);
  and and_29 (and_29_out, and_6_out, not_24_out);
  and and_30 (and_30_out, and_7_out, x4);
  and and_31 (and_31_out, x2, not_26_out);
  and and_32 (and_32_out, x2, x3);
  not not_42 (not_42_out, x4);
  and and_33 (and_33_out, h, not_27_out);
  not not_43 (not_43_out, x4);
  or or_2 (or_2_out, and_8_out, and_9_out);
  or or_3 (or_3_out, and_10_out, and_11_out);
  and and_34 (and_34_out, not_31_out, not_32_out);
  and and_35 (and_35_out, and_12_out, not_34_out);
  not not_44 (not_44_out, x4);
  not not_45 (not_45_out, x2);
  or or_4 (or_4_out, and_13_out, and_14_out);
  and and_36 (and_36_out, and_15_out, not_38_out);
  and and_37 (and_37_out, h, not_39_out);
  and and_38 (and_38_out, h, x4);
  or or_5 (or_5_out, and_16_out, and_17_out);
  and and_39 (and_39_out, and_18_out, x4);
  or or_6 (or_6_out, and_19_out, and_20_out);
  and and_40 (and_40_out, and_21_out, x3);
  or or_7 (or_7_out, and_22_out, and_23_out);
  and and_41 (and_41_out, not_40_out, not_41_out);
  and and_42 (and_42_out, and_24_out, x4);
  and and_43 (and_43_out, and_25_out, x4);
  or or_8 (or_8_out, or_1_out, and_26_out);
  or or_9 (or_9_out, and_27_out, and_28_out);
  or or_10 (or_10_out, and_29_out, and_30_out);
  and and_44 (and_44_out, and_31_out, x4);
  and and_45 (and_45_out, and_32_out, not_42_out);
  and and_46 (and_46_out, and_33_out, not_43_out);
  or or_11 (e, or_2_out, or_3_out);
  or or_12 (or_12_out, and_34_out, and_35_out);
  and and_47 (and_47_out, x2, not_44_out);
  and and_48 (and_48_out, h, not_45_out);
  and and_49 (and_49_out, h, x3);
  or or_13 (or_13_out, or_4_out, and_36_out);
  or or_14 (or_14_out, and_37_out, and_38_out);
  or or_15 (or_15_out, or_5_out, and_39_out);
  or or_16 (or_16_out, or_6_out, and_40_out);
  or or_17 (or_17_out, or_7_out, and_41_out);
  or or_18 (or_18_out, and_42_out, and_43_out);
  or or_19 (c, or_8_out, or_9_out);
  or or_20 (or_20_out, or_10_out, and_44_out);
  or or_21 (or_21_out, and_45_out, and_46_out);
  or or_22 (or_22_out, or_12_out, and_47_out);
  or or_23 (or_23_out, and_48_out, and_49_out);
  or or_24 (g, or_13_out, or_14_out);
  or or_25 (a, or_15_out, or_16_out);
  or or_26 (b, or_17_out, or_18_out);
  or or_27 (d, or_20_out, or_21_out);
  or or_28 (f, or_22_out, or_23_out);
endmodule

module display (
  input  a3,
  input  a2,
  input  a1,
  input  a0
);

  wire decodificador_1_a, decodificador_1_b, decodificador_1_c, decodificador_1_d, decodificador_1_e,
       decodificador_1_f, decodificador_1_g;

  decodificador decodificador_1 (
    .h(a3), .x2(a2), .x3(a1), .x4(a0), .a(decodificador_1_a), .b(decodificador_1_b), .c(decodificador_1_c),
    .d(decodificador_1_d), .e(decodificador_1_e), .f(decodificador_1_f), .g(decodificador_1_g));
  _7_Segment_Display u_7_segment_display_1 (
    .g(decodificador_1_g), .f(decodificador_1_f), .a(decodificador_1_a), .b(decodificador_1_b),
    .e(decodificador_1_e), .d(decodificador_1_d), .c(decodificador_1_c));  // open: dp
endmodule

module somadorCompleto1bit (
  input  a0,
  input  a1,
  input  c0,
  output s0,
  output carry_out
);

  wire somador_1_carry_out, somador_1_soma, somador_2_carry_out;

  somador somador_1 (.A0(a0), .B0(a1), .soma(somador_1_soma), .carry_out(somador_1_carry_out));
  somador somador_2 (.A0(somador_1_soma), .B0(c0), .soma(s0), .carry_out(somador_2_carry_out));
  or or_1 (carry_out, somador_2_carry_out, somador_1_carry_out);
endmodule

module somador4bits (
  input  c0,
  input  a0,
  input  a1,
  input  a2,
  input  a3,
  output s0,
  output s1,
  output carry_out
);

  wire somadorcompleto1bit_1_carry_out;

  somadorCompleto1bit somadorcompleto1bit_1 (
    .a0(a0), .a1(a1), .c0(c0), .s0(s0), .carry_out(somadorcompleto1bit_1_carry_out));
  somadorCompleto1bit somadorcompleto1bit_2 (
    .a0(a2), .a1(a3), .c0(somadorcompleto1bit_1_carry_out), .s0(s1), .carry_out(carry_out));
endmodule

// +
module somador8bits (
  input  c0,
  input  a3,
  input  a2,
  input  a1,
  input  a0,
  input  a3_2,
  input  a2_2,
  input  a1_2,
  input  a0_2,
  output s3,
  output s2,
  output s1,
  output s0,
  output carry_out
);

  wire somador4bits_1_carry_out;

  somador4bits somador4bits_1 (
    .c0(c0), .a0(a3), .a1(a2), .a2(a1), .a3(a0), .s0(s3), .s1(s2), .carry_out(somador4bits_1_carry_out));
  somador4bits somador4bits_2 (
    .c0(somador4bits_1_carry_out), .a0(a3_2), .a1(a2_2), .a2(a1_2), .a3(a0_2), .s0(s1), .s1(s0),
    .carry_out(carry_out));
endmodule

module calculadora (
  input  a3,
  input  a2,
  input  a1,
  input  a0,
  input  c0,
  input  b3,
  input  b2,
  input  b1,
  input  b0,
  output s3,
  output s2,
  output s1,
  output s0,
  output overflow
);

  wire decodificador_1_a, decodificador_1_b, decodificador_1_c, decodificador_1_d, decodificador_1_e,
       decodificador_1_f, decodificador_1_g, decodificador_2_a, decodificador_2_b, decodificador_2_c,
       decodificador_2_d, decodificador_2_e, decodificador_2_f, decodificador_2_g, decodificador_3_a,
       decodificador_3_b, decodificador_3_c, decodificador_3_d, decodificador_3_e, decodificador_3_f,
       decodificador_3_g;

  decodificador decodificador_1 (
    .h(a3), .x2(a2), .x3(a1), .x4(a0), .a(decodificador_1_a), .b(decodificador_1_b), .c(decodificador_1_c),
    .d(decodificador_1_d), .e(decodificador_1_e), .f(decodificador_1_f), .g(decodificador_1_g));
  somador8bits somador8bits_1 (
    .c0(c0), .a3(a3), .a2(a2), .a1(a1), .a0(a0), .a3_2(b3), .a2_2(b2), .a1_2(b1), .a0_2(b0), .s3(s3),
    .s2(s2), .s1(s1), .s0(s0), .carry_out(overflow));
  _7_Segment_Display u_7_segment_display_1 (
    .g(decodificador_1_g), .f(decodificador_1_f), .a(decodificador_1_a), .b(decodificador_1_b),
    .e(decodificador_1_e), .d(decodificador_1_d), .c(decodificador_1_c));  // open: dp
  decodificador decodificador_2 (
    .h(b3), .x2(b2), .x3(b1), .x4(b0), .a(decodificador_2_a), .b(decodificador_2_b), .c(decodificador_2_c),
    .d(decodificador_2_d), .e(decodificador_2_e), .f(decodificador_2_f), .g(decodificador_2_g));
  decodificador decodificador_3 (
    .h(s3), .x2(s2), .x3(s1), .x4(s0), .a(decodificador_3_a), .b(decodificador_3_b), .c(decodificador_3_c),
    .d(decodificador_3_d), .e(decodificador_3_e), .f(decodificador_3_f), .g(decodificador_3_g));
  _7_Segment_Display u_7_segment_display_2 (
    .g(decodificador_2_g), .f(decodificador_2_f), .a(decodificador_2_a), .b(decodificador_2_b),
    .e(decodificador_2_e), .d(decodificador_2_d), .c(decodificador_2_c));  // open: dp
  _7_Segment_Display u_7_segment_display_3 (
    .g(decodificador_3_g), .f(decodificador_3_f), .a(decodificador_3_a), .b(decodificador_3_b),
    .e(decodificador_3_e), .d(decodificador_3_d), .c(decodificador_3_c));  // open: dp
endmodule
